# Fritzing sketch gpio_input (saved by Fritzing 0.9.1b)
breadboards: 1

parts:
  BeagleBone1 = BeagleBone Black
  R1 = Resistor [tolerance=±5% resistance=10k package="0805 [SMD]"]
  S2 = Momentary Switch [package=tactile-pth]
  R2 = Resistor [tolerance=±5% resistance=10k package="0805 [SMD]"]

nets:
  N1: BeagleBone1.no_name_yet#7, S2.2
  N2: BeagleBone1.no_name_yet#24, R1.Pin_0
  N3: BeagleBone1.no_name_yet#45, R2.Pin_1
  N4: R1.Pin_1, S2.3, R2.Pin_0

custom parts:
  BeagleBone Black: BeagleBone Black rev. A5B
