# Fritzing sketch gpio_input_led (saved by Fritzing 0.9.1b)
breadboards: 2

parts:
  BeagleBone1 = BeagleBone Black
  R5 = Resistor [tolerance=±5% resistance=1k package="0805 [SMD]"]
  R6 = Resistor [tolerance=±5% resistance=10k package="0805 [SMD]"]
  R7 = Resistor [tolerance=±5% resistance=100 package="0805 [SMD]"]
  Q3 = NPN-Transistor [part_number=BC547 package="TO92 [THT]"]
  LED3 = smd LED [color="Red (633nm)" package="0603 [SMD]"]
  S3 = Momentary Switch [package=tactile-pth]
  R8 = Resistor [tolerance=±5% resistance=10k package="0805 [SMD]"]
  R9 = Resistor [tolerance=±5% resistance=100 package="0805 [SMD]"]

nets:
  N1: BeagleBone1.no_name_yet#5, S3.1
  N2: BeagleBone1.no_name_yet#10, R9.Pin_0
  N3: BeagleBone1.no_name_yet#24, R5.Pin_0, R6.Pin_0
  N4: BeagleBone1.no_name_yet#45, R6.Pin_1, Q3.E, R8.Pin_1
  N5: R5.Pin_1, Q3.B
  N6: R7.Pin_0, LED3.cathode
  N7: R7.Pin_1, Q3.C
  N8: S3.3, R8.Pin_0, R9.Pin_1

custom parts:
  BeagleBone Black: BeagleBone Black rev. A5B
