# Fritzing sketch adxl345 (saved by Fritzing 0.9.1b)

parts:
  BeagleBone1 = BeagleBone Black
  Part2 = Triple Axis Accelerometer Breakout - ADXL345

nets:
  N1: BeagleBone1.no_name_yet#1, Part2.GND
  N2: BeagleBone1.no_name_yet#7, Part2.VCC, Part2.CS
  N3: BeagleBone1.no_name_yet#17, Part2.SCL
  N4: BeagleBone1.no_name_yet#18, Part2.SDA

custom parts:
  BeagleBone Black: BeagleBone Black rev. A5B
