# Fritzing sketch led8x8matrix (saved by Fritzing 0.9.0b)

parts:
  BeagleBone1 = BeagleBone Black
  LED1 = 8x8 LED Matrix (green)

nets:
  N1: BeagleBone1.no_name_yet#1, LED1.-
  N2: BeagleBone1.no_name_yet#7, LED1.+
  N3: BeagleBone1.no_name_yet#19, LED1.C
  N4: BeagleBone1.no_name_yet#20, LED1.D

custom parts:
  BeagleBone Black: BeagleBone Black rev. A5B
  8x8 LED Matrix (green): 8x8 LED Matrix with I2C control (green)
