# Fritzing sketch adxl345 (saved by Fritzing 0.9.0b)

parts:
  BeagleBone1 = BeagleBone Black
  Part2 = Triple Axis Accelerometer Breakout - ADXL345

nets:
  N1: BeagleBone1.no_name_yet#1, Part2.GND
  N2: BeagleBone1.no_name_yet#7, Part2.VCC
  N3: BeagleBone1.no_name_yet#17, Part2.CS
  N4: BeagleBone1.no_name_yet#18, Part2.SDA
  N5: BeagleBone1.no_name_yet#21, Part2.SDO
  N6: BeagleBone1.no_name_yet#22, Part2.SCL

custom parts:
  BeagleBone Black: BeagleBone Black rev. A5B
