# Fritzing sketch mcp23s08 (saved by Fritzing 0.9.0b)
breadboards: 1

parts:
  BeagleBone1 = BeagleBone Black
  D1 = LED_BARGRAPH_10 [package=led_bargaph_10]
  Q1 = MCP23S08 [part_number=MCP23S08]
  R1 = Resistor [package="2010 [SMD]"]
  R2 = Resistor [package="2010 [SMD]"]
  R3 = Resistor [package="2010 [SMD]"]
  R4 = Resistor [package="2010 [SMD]"]
  R5 = Resistor [package="2010 [SMD]"]
  R6 = Resistor [package="2010 [SMD]"]
  R7 = Resistor [package="2010 [SMD]"]
  R8 = Resistor [package="2010 [SMD]"]

nets:
  N1: BeagleBone1.no_name_yet#1, D1.A_A, D1.B_A, D1.C_A, D1.D_A, D1.E_A, D1.F_A, D1.G_A, D1.H_A, Q1.A1, Q1.A0, Q1.VSS
  N2: BeagleBone1.no_name_yet#7, Q1.RESET, Q1.VDD
  N3: BeagleBone1.no_name_yet#17, Q1.CS
  N4: BeagleBone1.no_name_yet#18, Q1.SI
  N5: BeagleBone1.no_name_yet#21, Q1.SO
  N6: BeagleBone1.no_name_yet#22, Q1.SCK
  N7: D1.H_C, R5.Pin_0
  N8: D1.G_C, R6.Pin_0
  N9: D1.F_C, R7.Pin_0
  N10: D1.E_C, R8.Pin_0
  N11: D1.D_C, D1.C_C, D1.B_C, D1.A_C, R1.Pin_1, R2.Pin_1, R3.Pin_1, R4.Pin_1
  N12: Q1.GPIO0, Q1.GPIO1, Q1.GPIO2, Q1.GPIO3, R1.Pin_0, R2.Pin_0, R3.Pin_0, R4.Pin_0
  N13: Q1.GPIO4, R8.Pin_1
  N14: Q1.GPIO5, R7.Pin_1
  N15: Q1.GPIO6, R6.Pin_1
  N16: Q1.GPIO7, R5.Pin_1

custom parts:
  BeagleBone Black: BeagleBone Black rev. A5B
  MCP23S08: MCP23S08 8-Bit I/O Expander with Serial Interface
