# Fritzing sketch mcp23s08_mcp4902 (saved by Fritzing 0.9.1b)
breadboards: 1

parts:
  BeagleBone1 = BeagleBone Black
  Q1 = MCP23S08 [part_number=MCP23S08]
  IC2 = DIP - 14 pins [chip_label=MCP4902 package="DIP (Dual Inline) [THT]"]
  LED2 = smd LED [color="Red (633nm)" package="1206 [SMD]"]
  LED3 = smd LED [color="Red (633nm)" package="1206 [SMD]"]

nets:
  N1: BeagleBone1.no_name_yet#17, Q1.CS
  N2: BeagleBone1.no_name_yet#18, Q1.SI
  N3: BeagleBone1.no_name_yet#21, Q1.SO
  N4: BeagleBone1.no_name_yet#22, Q1.SCK
  N5: Q1.A1, Q1.A0, Q1.VSS, LED2.anode, LED3.anode
  VDD: Q1.RESET, Q1.VDD, IC2.VDD, IC2./SHDN, IC2.VREFB, IC2.VREFA
  N6: Q1.GPIO0, IC2./CS
  N7: Q1.GPIO4, IC2.SCK
  N8: Q1.GPIO5, IC2.SDI
  N9: IC2./LDAC, IC2.VSS
  N10: IC2.VOUTB, LED3.cathode
  N11: IC2.VOUTA, LED2.cathode

custom parts:
  BeagleBone Black: BeagleBone Black rev. A5B
  MCP23S08: MCP23S08 8-Bit I/O Expander with Serial Interface
  DIP - 14 pins: A DIP stand-in part for whatever IC you want. With 14 pins on a 300mil dual inline package (DIP) footprint.
