# Fritzing sketch mcp4902 (saved by Fritzing 0.9.1b)
breadboards: 1

parts:
  IC1 = DIP - 14 pins [chip_label=MCP4902 package="DIP (Dual Inline) [THT]"]
  LED1 = smd LED [color="Red (633nm)" package="1206 [SMD]"]
  LED2 = smd LED [color="Red (633nm)" package="1206 [SMD]"]
  BeagleBone1 = BeagleBone Black

nets:
  N1: IC1.VDD, IC1./SHDN, IC1.VREFB, IC1.VREFA, BeagleBone1.no_name_yet#7
  N2: IC1./CS, BeagleBone1.no_name_yet#17
  N3: IC1.SCK, BeagleBone1.no_name_yet#22
  N4: IC1.SDI, BeagleBone1.no_name_yet#18
  N5: IC1./LDAC, IC1.VSS, LED1.anode, LED2.anode, BeagleBone1.no_name_yet#1
  N6: IC1.VOUTB, LED2.cathode
  N7: IC1.VOUTA, LED1.cathode

custom parts:
  DIP - 14 pins: A DIP stand-in part for whatever IC you want. With 14 pins on a 300mil dual inline package (DIP) footprint.
  BeagleBone Black: BeagleBone Black rev. A5B
